// Logisim project MiniCalc.circ as structural Verilog: 3 circuits, main circuit 1G3157
module MiniCalc (
  input  RUN,
  input  SUB_ADD,
  input  DIV_MUL,
  input  [7:0] Input_A,
  input  [4:0] Input_B,
  input  [4:0] Input_X,
  output [9:0] ACCUMULATOR,
  output [4:0] COUNT
);

  wire ADD, CLK, CONTINUE_DIV, CONTINUE_MUL, DIV, EXEC, MUL, n1g3157_2_out_4, n1g3157_4_out_4, n1g3157_6_o,
       n1g3157_7_o, n1g3157_8_o, n1g3157_9_o, n1g3157_10_o, n1g3157_11_o, n1g3157_11_out_4, n1g3157_12_o,
       n1g3157_13_o, n1g3157_13_out_4, n1g3157_14_o, n1g3157_15_o, n1g3157_15_out_4, n1g3157_16_o,
       n1g3157_17_o, n1g3157_17_out_4, n1g3157_18_o, n1g3157_19_out_4, n1g3157_20_o, n1g3157_21_o,
       n1g3157_23_o, n1g3157_24_o, n1g3157_25_o, n1g3157_26_o, n1g3157_27_o, n1g3157_28_o, n1g3157_29_o,
       n1g3157_30_o, n1g3157_31_o, n1g3157_32_o, n1g3157_34_o, n1g3157_35_o, n1g3157_36_o, n1g3157_37_o,
       n1g3157_38_o, n1g3157_39_o, n1g3157_40_o, n1g3157_41_o, n1g3157_42_o, n1g3157_43_o, n1g3157_49_o,
       n1g3157_49_out_4, n1g3157_50_o, n1g3157_51_o, n1g3157_52_o, n1g3157_52_out_4, n1g3157_53_o,
       n1g3157_54_o, n1g3157_55_o, n1g3157_55_out_4, n1g3157_56_o, n1g3157_57_o, n1g3157_58_o,
       n1g3157_58_out_4, n1g3157_59_o, n1g3157_60_o, n1g3157_61_o, n1g3157_61_out_4, n1g3157_62_o,
       n1g3157_63_o, n1g3157_64_o, n1g3157_64_out_4, n1g3157_65_o, n1g3157_66_o, n1g3157_67_o,
       n1g3157_67_out_4, n1g3157_68_o, n1g3157_69_o, n1g3157_70_o, n1g3157_70_out_4, n1g3157_71_o,
       n1g3157_72_o, n1g3157_73_o, n1g3157_73_out_4, n1g3157_74_o, n1g3157_75_o, n1g3157_76_o,
       n1g3157_76_out_4, n1g3157_77_o, n1g3157_78_o, n1g3157_79_o, n1g3157_80_o, n1g3157_81_o, n1g3157_82_o,
       n1g3157_83_o, n1g3157_84_o, n1g3157_85_o, n1g3157_86_o, n1g3157_87_o, n1g3157_88_o, n1g3157_89_o,
       n1g3157_89_out_4, n1g3157_90_o, n1g3157_91_o, n1g3157_91_out_4, n1g3157_92_o, n1g3157_93_o,
       n1g3157_93_out_4, n1g3157_94_o, n1g3157_95_o, n1g3157_95_out_4, n1g3157_96_o, n1g3157_97_o,
       n1g3157_97_out_4, n1g3157_98_o, n1g3157_99_o, n1g3157_99_out_4, n1g3157_100_o, n1g3157_101_o,
       n1g3157_101_out_4, n1g3157_102_o, n1g3157_103_o, n1g3157_103_out_4, n1g3157_104_o, n1g3157_105_o,
       n1g3157_105_out_4, n1g3157_106_o, n1g3157_107_out_4, n1g3157_108_o, n1g3157_109_o, n1g3157_110_o,
       n1g3157_111_o, n1g3157_112_o, n1g3157_113_o, n1g3157_114_o, n1g3157_115_o, n1g3157_116_o,
       n1g3157_117_o, n1g3157_118_o, n1g3157_119_o, n1g3157_120_o, n1g3157_121_o, n1g3157_122_o,
       n1g3157_123_o, n1g3157_124_o, n1g3157_125_o, n1g3157_126_o, n1g3157_127_o, n1g3157_128_o,
       n1g3157_129_o, n1g3157_130_o, n1g3157_131_o, n1g3157_132_o, n1g3157_133_o, n1g3157_134_o,
       n1g3157_135_o, n1g3157_136_o, n1g3157_137_o, n1g3157_138_o, n1g3157_139_o, n1g3157_140_o,
       n1g3157_141_o, n1g3157_142_o, n1g3157_143_o, n1g3157_144_o, n1g3157_145_o, n1g3157_146_o,
       n1g3157_147_o, n1g3157_148_o, oscilator_1_ck, P_2_o, P_3_o, P_4_o, P_5_o, P_o, RUN_t, SUB;

  _1G3157 u_1g3157_1 (.O(RUN_t), .S(RUN), .Y0(1'b0), .Y1(1'b1));  // open: out_4
  _1G3157 u_1g3157_2 (.out_4(n1g3157_2_out_4), .O(SUB), .S(SUB_ADD), .Y0(1'b0), .Y1(1'b1));
  _1G3157 u_1g3157_3 (.O(ADD), .S(n1g3157_2_out_4), .Y0(1'b1), .Y1(1'b0));  // open: out_4
  _1G3157 u_1g3157_4 (.out_4(n1g3157_4_out_4), .O(DIV), .S(DIV_MUL), .Y0(1'b0), .Y1(1'b1));
  _1G3157 u_1g3157_5 (.O(MUL), .S(n1g3157_4_out_4), .Y0(1'b1), .Y1(1'b0));  // open: out_4
  _1G3157 u_1g3157_6 (.O(n1g3157_6_o), .S(DIV), .Y0(1'b1), .Y1(1'b0));  // open: out_4
  _1G3157 u_1g3157_7 (.O(n1g3157_7_o), .S(n1g3157_11_o), .Y0(1'b1), .Y1(1'b0));  // open: out_4
  _1G3157 u_1g3157_8 (.O(n1g3157_8_o), .S(n1g3157_13_o), .Y0(1'b1), .Y1(1'b0));  // open: out_4
  _1G3157 u_1g3157_9 (.O(n1g3157_9_o), .S(n1g3157_15_o), .Y0(1'b1), .Y1(1'b0));  // open: out_4
  _1G3157 u_1g3157_10 (.O(n1g3157_10_o), .S(n1g3157_17_o), .Y0(1'b1), .Y1(1'b0));  // open: out_4
  _1G3157 P (.O(P_o), .S(COUNT[0]), .Y0(MUL), .Y1(DIV));  // open: out_4
  _1G3157 P_2 (.O(P_2_o), .S(COUNT[1]), .Y0(MUL), .Y1(DIV));  // open: out_4
  _1G3157 P_3 (.O(P_3_o), .S(COUNT[2]), .Y0(MUL), .Y1(DIV));  // open: out_4
  _1G3157 P_4 (.O(P_4_o), .S(COUNT[3]), .Y0(MUL), .Y1(DIV));  // open: out_4
  _1G3157 P_5 (.O(P_5_o), .S(COUNT[4]), .Y0(MUL), .Y1(DIV));  // open: out_4
  _1G3157 u_1g3157_11 (.out_4(n1g3157_11_out_4), .O(n1g3157_11_o), .S(P_o), .Y0(MUL), .Y1(DIV));
  _1G3157 u_1g3157_12 (.O(n1g3157_12_o), .S(n1g3157_11_out_4), .Y0(DIV), .Y1(n1g3157_6_o));  // open: out_4
  _1G3157 u_1g3157_13 (.out_4(n1g3157_13_out_4), .O(n1g3157_13_o), .S(P_2_o), .Y0(MUL), .Y1(n1g3157_11_o));
  _1G3157 u_1g3157_14 (.O(n1g3157_14_o), .S(n1g3157_13_out_4), .Y0(n1g3157_11_o), .Y1(n1g3157_7_o));  // open: out_4
  _1G3157 u_1g3157_15 (.out_4(n1g3157_15_out_4), .O(n1g3157_15_o), .S(P_3_o), .Y0(MUL), .Y1(n1g3157_13_o));
  _1G3157 u_1g3157_16 (.O(n1g3157_16_o), .S(n1g3157_15_out_4), .Y0(n1g3157_13_o), .Y1(n1g3157_8_o));  // open: out_4
  _1G3157 u_1g3157_17 (.out_4(n1g3157_17_out_4), .O(n1g3157_17_o), .S(P_4_o), .Y0(MUL), .Y1(n1g3157_15_o));
  _1G3157 u_1g3157_18 (.O(n1g3157_18_o), .S(n1g3157_17_out_4), .Y0(n1g3157_15_o), .Y1(n1g3157_9_o));  // open: out_4
  _1G3157 u_1g3157_19 (.out_4(n1g3157_19_out_4), .O(CONTINUE_MUL), .S(P_5_o), .Y0(MUL), .Y1(n1g3157_17_o));
  _1G3157 u_1g3157_20 (.O(n1g3157_20_o), .S(n1g3157_19_out_4), .Y0(n1g3157_17_o), .Y1(n1g3157_10_o));  // open: out_4
  LED u_EXEC (.in(EXEC));
  _1G3157 u_1g3157_21 (.O(n1g3157_21_o), .S(DIV), .Y0(CONTINUE_MUL), .Y1(CONTINUE_DIV));  // open: out_4
  _1G3157 u_1g3157_22 (.O(EXEC), .S(n1g3157_21_o), .Y0(1'b0), .Y1(RUN_t));  // open: out_4
  _1G3157 u_1g3157_23 (.O(n1g3157_23_o), .S(CLK), .Y0(n1g3157_12_o), .Y1(n1g3157_28_o));  // open: out_4
  _1G3157 u_1g3157_24 (.O(n1g3157_24_o), .S(CLK), .Y0(n1g3157_14_o), .Y1(n1g3157_29_o));  // open: out_4
  _1G3157 u_1g3157_25 (.O(n1g3157_25_o), .S(CLK), .Y0(n1g3157_16_o), .Y1(n1g3157_30_o));  // open: out_4
  _1G3157 u_1g3157_26 (.O(n1g3157_26_o), .S(CLK), .Y0(n1g3157_18_o), .Y1(n1g3157_31_o));  // open: out_4
  _1G3157 u_1g3157_27 (.O(n1g3157_27_o), .S(CLK), .Y0(n1g3157_20_o), .Y1(n1g3157_32_o));  // open: out_4
  Oscilator oscilator_1 (.CK(oscilator_1_ck), .E(EXEC));
  _1G3157 u_1g3157_28 (.O(n1g3157_28_o), .S(n1g3157_23_o), .Y0(1'b0), .Y1(1'b1));  // open: out_4
  _1G3157 u_1g3157_29 (.O(n1g3157_29_o), .S(n1g3157_24_o), .Y0(1'b0), .Y1(1'b1));  // open: out_4
  _1G3157 u_1g3157_30 (.O(n1g3157_30_o), .S(n1g3157_25_o), .Y0(1'b0), .Y1(1'b1));  // open: out_4
  _1G3157 u_1g3157_31 (.O(n1g3157_31_o), .S(n1g3157_26_o), .Y0(1'b0), .Y1(1'b1));  // open: out_4
  _1G3157 u_1g3157_32 (.O(n1g3157_32_o), .S(n1g3157_27_o), .Y0(1'b0), .Y1(1'b1));  // open: out_4
  _1G3157 u_1g3157_33 (.O(CLK), .S(oscilator_1_ck), .Y0(1'b0), .Y1(1'b1));  // open: out_4
  _1G3157 u_1g3157_34 (.O(n1g3157_34_o), .S(CLK), .Y0(COUNT[0]), .Y1(n1g3157_28_o));  // open: out_4
  _1G3157 u_1g3157_35 (.O(n1g3157_35_o), .S(CLK), .Y0(COUNT[1]), .Y1(n1g3157_29_o));  // open: out_4
  _1G3157 u_1g3157_36 (.O(n1g3157_36_o), .S(CLK), .Y0(COUNT[2]), .Y1(n1g3157_30_o));  // open: out_4
  _1G3157 u_1g3157_37 (.O(n1g3157_37_o), .S(CLK), .Y0(COUNT[3]), .Y1(n1g3157_31_o));  // open: out_4
  _1G3157 u_1g3157_38 (.O(n1g3157_38_o), .S(CLK), .Y0(COUNT[4]), .Y1(n1g3157_32_o));  // open: out_4
  _1G3157 u_1g3157_39 (.O(n1g3157_39_o), .S(RUN_t), .Y0(Input_X[0]), .Y1(n1g3157_34_o));  // open: out_4
  _1G3157 u_1g3157_40 (.O(n1g3157_40_o), .S(RUN_t), .Y0(Input_X[1]), .Y1(n1g3157_35_o));  // open: out_4
  _1G3157 u_1g3157_41 (.O(n1g3157_41_o), .S(RUN_t), .Y0(Input_X[2]), .Y1(n1g3157_36_o));  // open: out_4
  _1G3157 u_1g3157_42 (.O(n1g3157_42_o), .S(RUN_t), .Y0(Input_X[3]), .Y1(n1g3157_37_o));  // open: out_4
  _1G3157 u_1g3157_43 (.O(n1g3157_43_o), .S(RUN_t), .Y0(Input_X[4]), .Y1(n1g3157_38_o));  // open: out_4
  _1G3157 u_1g3157_44 (.O(COUNT[0]), .S(n1g3157_39_o), .Y0(1'b0), .Y1(1'b1));  // open: out_4
  _1G3157 u_1g3157_45 (.O(COUNT[1]), .S(n1g3157_40_o), .Y0(1'b0), .Y1(1'b1));  // open: out_4
  _1G3157 u_1g3157_46 (.O(COUNT[2]), .S(n1g3157_41_o), .Y0(1'b0), .Y1(1'b1));  // open: out_4
  _1G3157 u_1g3157_47 (.O(COUNT[3]), .S(n1g3157_42_o), .Y0(1'b0), .Y1(1'b1));  // open: out_4
  _1G3157 u_1g3157_48 (.O(COUNT[4]), .S(n1g3157_43_o), .Y0(1'b0), .Y1(1'b1));  // open: out_4
  _1G3157 u_1g3157_49 (.out_4(n1g3157_49_out_4), .O(n1g3157_49_o), .S(Input_B[0]), .Y0(ADD), .Y1(SUB));
  _1G3157 u_1g3157_50 (.O(n1g3157_50_o), .S(n1g3157_49_out_4), .Y0(SUB), .Y1(ADD));  // open: out_4
  _1G3157 u_1g3157_51 (.O(n1g3157_51_o), .S(SUB), .Y0(1'b1), .Y1(1'b0));  // open: out_4
  _1G3157 u_1g3157_52 (.out_4(n1g3157_52_out_4), .O(n1g3157_52_o), .S(Input_B[1]), .Y0(ADD), .Y1(SUB));
  _1G3157 u_1g3157_53 (.O(n1g3157_53_o), .S(n1g3157_52_out_4), .Y0(SUB), .Y1(ADD));  // open: out_4
  _1G3157 u_1g3157_54 (.O(n1g3157_54_o), .S(n1g3157_89_o), .Y0(1'b1), .Y1(1'b0));  // open: out_4
  _1G3157 u_1g3157_55 (.out_4(n1g3157_55_out_4), .O(n1g3157_55_o), .S(Input_B[2]), .Y0(ADD), .Y1(SUB));
  _1G3157 u_1g3157_56 (.O(n1g3157_56_o), .S(n1g3157_55_out_4), .Y0(SUB), .Y1(ADD));  // open: out_4
  _1G3157 u_1g3157_57 (.O(n1g3157_57_o), .S(n1g3157_91_o), .Y0(1'b1), .Y1(1'b0));  // open: out_4
  _1G3157 u_1g3157_58 (.out_4(n1g3157_58_out_4), .O(n1g3157_58_o), .S(Input_B[3]), .Y0(ADD), .Y1(SUB));
  _1G3157 u_1g3157_59 (.O(n1g3157_59_o), .S(n1g3157_58_out_4), .Y0(SUB), .Y1(ADD));  // open: out_4
  _1G3157 u_1g3157_60 (.O(n1g3157_60_o), .S(n1g3157_93_o), .Y0(1'b1), .Y1(1'b0));  // open: out_4
  _1G3157 u_1g3157_61 (.out_4(n1g3157_61_out_4), .O(n1g3157_61_o), .S(Input_B[4]), .Y0(ADD), .Y1(SUB));
  _1G3157 u_1g3157_62 (.O(n1g3157_62_o), .S(n1g3157_61_out_4), .Y0(SUB), .Y1(ADD));  // open: out_4
  _1G3157 u_1g3157_63 (.O(n1g3157_63_o), .S(n1g3157_95_o), .Y0(1'b1), .Y1(1'b0));  // open: out_4
  _1G3157 u_1g3157_64 (.out_4(n1g3157_64_out_4), .O(n1g3157_64_o), .S(1'b0), .Y0(ADD), .Y1(SUB));
  _1G3157 u_1g3157_65 (.O(n1g3157_65_o), .S(n1g3157_64_out_4), .Y0(SUB), .Y1(ADD));  // open: out_4
  _1G3157 u_1g3157_66 (.O(n1g3157_66_o), .S(n1g3157_97_o), .Y0(1'b1), .Y1(1'b0));  // open: out_4
  _1G3157 u_1g3157_67 (.out_4(n1g3157_67_out_4), .O(n1g3157_67_o), .S(1'b0), .Y0(ADD), .Y1(SUB));
  _1G3157 u_1g3157_68 (.O(n1g3157_68_o), .S(n1g3157_67_out_4), .Y0(SUB), .Y1(ADD));  // open: out_4
  _1G3157 u_1g3157_69 (.O(n1g3157_69_o), .S(n1g3157_99_o), .Y0(1'b1), .Y1(1'b0));  // open: out_4
  _1G3157 u_1g3157_70 (.out_4(n1g3157_70_out_4), .O(n1g3157_70_o), .S(1'b0), .Y0(ADD), .Y1(SUB));
  _1G3157 u_1g3157_71 (.O(n1g3157_71_o), .S(n1g3157_70_out_4), .Y0(SUB), .Y1(ADD));  // open: out_4
  _1G3157 u_1g3157_72 (.O(n1g3157_72_o), .S(n1g3157_101_o), .Y0(1'b1), .Y1(1'b0));  // open: out_4
  _1G3157 u_1g3157_73 (.out_4(n1g3157_73_out_4), .O(n1g3157_73_o), .S(1'b0), .Y0(ADD), .Y1(SUB));
  _1G3157 u_1g3157_74 (.O(n1g3157_74_o), .S(n1g3157_73_out_4), .Y0(SUB), .Y1(ADD));  // open: out_4
  _1G3157 u_1g3157_75 (.O(n1g3157_75_o), .S(n1g3157_103_o), .Y0(1'b1), .Y1(1'b0));  // open: out_4
  _1G3157 u_1g3157_76 (.out_4(n1g3157_76_out_4), .O(n1g3157_76_o), .S(1'b0), .Y0(ADD), .Y1(SUB));
  _1G3157 u_1g3157_77 (.O(n1g3157_77_o), .S(n1g3157_76_out_4), .Y0(SUB), .Y1(ADD));  // open: out_4
  _1G3157 u_1g3157_78 (.O(n1g3157_78_o), .S(n1g3157_105_o), .Y0(1'b1), .Y1(1'b0));  // open: out_4
  _1G3157 u_1g3157_79 (.O(n1g3157_79_o), .S(ACCUMULATOR[0]), .Y0(n1g3157_50_o), .Y1(n1g3157_49_o));  // open: out_4
  _1G3157 u_1g3157_80 (.O(n1g3157_80_o), .S(ACCUMULATOR[1]), .Y0(n1g3157_53_o), .Y1(n1g3157_52_o));  // open: out_4
  _1G3157 u_1g3157_81 (.O(n1g3157_81_o), .S(ACCUMULATOR[2]), .Y0(n1g3157_56_o), .Y1(n1g3157_55_o));  // open: out_4
  _1G3157 u_1g3157_82 (.O(n1g3157_82_o), .S(ACCUMULATOR[3]), .Y0(n1g3157_59_o), .Y1(n1g3157_58_o));  // open: out_4
  _1G3157 u_1g3157_83 (.O(n1g3157_83_o), .S(ACCUMULATOR[4]), .Y0(n1g3157_62_o), .Y1(n1g3157_61_o));  // open: out_4
  _1G3157 u_1g3157_84 (.O(n1g3157_84_o), .S(ACCUMULATOR[5]), .Y0(n1g3157_65_o), .Y1(n1g3157_64_o));  // open: out_4
  _1G3157 u_1g3157_85 (.O(n1g3157_85_o), .S(ACCUMULATOR[6]), .Y0(n1g3157_68_o), .Y1(n1g3157_67_o));  // open: out_4
  _1G3157 u_1g3157_86 (.O(n1g3157_86_o), .S(ACCUMULATOR[7]), .Y0(n1g3157_71_o), .Y1(n1g3157_70_o));  // open: out_4
  _1G3157 u_1g3157_87 (.O(n1g3157_87_o), .S(ACCUMULATOR[8]), .Y0(n1g3157_74_o), .Y1(n1g3157_73_o));  // open: out_4
  _1G3157 u_1g3157_88 (.O(n1g3157_88_o), .S(ACCUMULATOR[9]), .Y0(n1g3157_77_o), .Y1(n1g3157_76_o));  // open: out_4
  _1G3157 u_1g3157_89 (.out_4(n1g3157_89_out_4), .O(n1g3157_89_o), .S(n1g3157_79_o), .Y0(n1g3157_50_o), .Y1(SUB));
  _1G3157 u_1g3157_90 (.O(n1g3157_90_o), .S(n1g3157_89_out_4), .Y0(SUB), .Y1(n1g3157_51_o));  // open: out_4
  _1G3157 u_1g3157_91 (
    .out_4(n1g3157_91_out_4), .O(n1g3157_91_o), .S(n1g3157_80_o), .Y0(n1g3157_53_o), .Y1(n1g3157_89_o));
  _1G3157 u_1g3157_92 (.O(n1g3157_92_o), .S(n1g3157_91_out_4), .Y0(n1g3157_89_o), .Y1(n1g3157_54_o));  // open: out_4
  _1G3157 u_1g3157_93 (
    .out_4(n1g3157_93_out_4), .O(n1g3157_93_o), .S(n1g3157_81_o), .Y0(n1g3157_56_o), .Y1(n1g3157_91_o));
  _1G3157 u_1g3157_94 (.O(n1g3157_94_o), .S(n1g3157_93_out_4), .Y0(n1g3157_91_o), .Y1(n1g3157_57_o));  // open: out_4
  _1G3157 u_1g3157_95 (
    .out_4(n1g3157_95_out_4), .O(n1g3157_95_o), .S(n1g3157_82_o), .Y0(n1g3157_59_o), .Y1(n1g3157_93_o));
  _1G3157 u_1g3157_96 (.O(n1g3157_96_o), .S(n1g3157_95_out_4), .Y0(n1g3157_93_o), .Y1(n1g3157_60_o));  // open: out_4
  _1G3157 u_1g3157_97 (
    .out_4(n1g3157_97_out_4), .O(n1g3157_97_o), .S(n1g3157_83_o), .Y0(n1g3157_62_o), .Y1(n1g3157_95_o));
  _1G3157 u_1g3157_98 (.O(n1g3157_98_o), .S(n1g3157_97_out_4), .Y0(n1g3157_95_o), .Y1(n1g3157_63_o));  // open: out_4
  _1G3157 u_1g3157_99 (
    .out_4(n1g3157_99_out_4), .O(n1g3157_99_o), .S(n1g3157_84_o), .Y0(n1g3157_65_o), .Y1(n1g3157_97_o));
  _1G3157 u_1g3157_100 (.O(n1g3157_100_o), .S(n1g3157_99_out_4), .Y0(n1g3157_97_o), .Y1(n1g3157_66_o));  // open: out_4
  _1G3157 u_1g3157_101 (
    .out_4(n1g3157_101_out_4), .O(n1g3157_101_o), .S(n1g3157_85_o), .Y0(n1g3157_68_o), .Y1(n1g3157_99_o));
  _1G3157 u_1g3157_102 (.O(n1g3157_102_o), .S(n1g3157_101_out_4), .Y0(n1g3157_99_o), .Y1(n1g3157_69_o));  // open: out_4
  _1G3157 u_1g3157_103 (
    .out_4(n1g3157_103_out_4), .O(n1g3157_103_o), .S(n1g3157_86_o), .Y0(n1g3157_71_o), .Y1(n1g3157_101_o));
  _1G3157 u_1g3157_104 (
    .O(n1g3157_104_o), .S(n1g3157_103_out_4), .Y0(n1g3157_101_o), .Y1(n1g3157_72_o));  // open: out_4
  _1G3157 u_1g3157_105 (
    .out_4(n1g3157_105_out_4), .O(n1g3157_105_o), .S(n1g3157_87_o), .Y0(n1g3157_74_o), .Y1(n1g3157_103_o));
  _1G3157 u_1g3157_106 (
    .O(n1g3157_106_o), .S(n1g3157_105_out_4), .Y0(n1g3157_103_o), .Y1(n1g3157_75_o));  // open: out_4
  _1G3157 u_1g3157_107 (
    .out_4(n1g3157_107_out_4), .O(CONTINUE_DIV), .S(n1g3157_88_o), .Y0(n1g3157_77_o), .Y1(n1g3157_105_o));
  _1G3157 u_1g3157_108 (
    .O(n1g3157_108_o), .S(n1g3157_107_out_4), .Y0(n1g3157_105_o), .Y1(n1g3157_78_o));  // open: out_4
  _1G3157 u_1g3157_109 (.O(n1g3157_109_o), .S(CLK), .Y0(n1g3157_90_o), .Y1(n1g3157_119_o));  // open: out_4
  _1G3157 u_1g3157_110 (.O(n1g3157_110_o), .S(CLK), .Y0(n1g3157_92_o), .Y1(n1g3157_120_o));  // open: out_4
  _1G3157 u_1g3157_111 (.O(n1g3157_111_o), .S(CLK), .Y0(n1g3157_94_o), .Y1(n1g3157_121_o));  // open: out_4
  _1G3157 u_1g3157_112 (.O(n1g3157_112_o), .S(CLK), .Y0(n1g3157_96_o), .Y1(n1g3157_122_o));  // open: out_4
  _1G3157 u_1g3157_113 (.O(n1g3157_113_o), .S(CLK), .Y0(n1g3157_98_o), .Y1(n1g3157_123_o));  // open: out_4
  _1G3157 u_1g3157_114 (.O(n1g3157_114_o), .S(CLK), .Y0(n1g3157_100_o), .Y1(n1g3157_124_o));  // open: out_4
  _1G3157 u_1g3157_115 (.O(n1g3157_115_o), .S(CLK), .Y0(n1g3157_102_o), .Y1(n1g3157_125_o));  // open: out_4
  _1G3157 u_1g3157_116 (.O(n1g3157_116_o), .S(CLK), .Y0(n1g3157_104_o), .Y1(n1g3157_126_o));  // open: out_4
  _1G3157 u_1g3157_117 (.O(n1g3157_117_o), .S(CLK), .Y0(n1g3157_106_o), .Y1(n1g3157_127_o));  // open: out_4
  _1G3157 u_1g3157_118 (.O(n1g3157_118_o), .S(CLK), .Y0(n1g3157_108_o), .Y1(n1g3157_128_o));  // open: out_4
  _1G3157 u_1g3157_119 (.O(n1g3157_119_o), .S(n1g3157_109_o), .Y0(1'b0), .Y1(1'b1));  // open: out_4
  _1G3157 u_1g3157_120 (.O(n1g3157_120_o), .S(n1g3157_110_o), .Y0(1'b0), .Y1(1'b1));  // open: out_4
  _1G3157 u_1g3157_121 (.O(n1g3157_121_o), .S(n1g3157_111_o), .Y0(1'b0), .Y1(1'b1));  // open: out_4
  _1G3157 u_1g3157_122 (.O(n1g3157_122_o), .S(n1g3157_112_o), .Y0(1'b0), .Y1(1'b1));  // open: out_4
  _1G3157 u_1g3157_123 (.O(n1g3157_123_o), .S(n1g3157_113_o), .Y0(1'b0), .Y1(1'b1));  // open: out_4
  _1G3157 u_1g3157_124 (.O(n1g3157_124_o), .S(n1g3157_114_o), .Y0(1'b0), .Y1(1'b1));  // open: out_4
  _1G3157 u_1g3157_125 (.O(n1g3157_125_o), .S(n1g3157_115_o), .Y0(1'b0), .Y1(1'b1));  // open: out_4
  _1G3157 u_1g3157_126 (.O(n1g3157_126_o), .S(n1g3157_116_o), .Y0(1'b0), .Y1(1'b1));  // open: out_4
  _1G3157 u_1g3157_127 (.O(n1g3157_127_o), .S(n1g3157_117_o), .Y0(1'b0), .Y1(1'b1));  // open: out_4
  _1G3157 u_1g3157_128 (.O(n1g3157_128_o), .S(n1g3157_118_o), .Y0(1'b0), .Y1(1'b1));  // open: out_4
  _1G3157 u_1g3157_129 (.O(n1g3157_129_o), .S(CLK), .Y0(ACCUMULATOR[0]), .Y1(n1g3157_119_o));  // open: out_4
  _1G3157 u_1g3157_130 (.O(n1g3157_130_o), .S(CLK), .Y0(ACCUMULATOR[1]), .Y1(n1g3157_120_o));  // open: out_4
  _1G3157 u_1g3157_131 (.O(n1g3157_131_o), .S(CLK), .Y0(ACCUMULATOR[2]), .Y1(n1g3157_121_o));  // open: out_4
  _1G3157 u_1g3157_132 (.O(n1g3157_132_o), .S(CLK), .Y0(ACCUMULATOR[3]), .Y1(n1g3157_122_o));  // open: out_4
  _1G3157 u_1g3157_133 (.O(n1g3157_133_o), .S(CLK), .Y0(ACCUMULATOR[4]), .Y1(n1g3157_123_o));  // open: out_4
  _1G3157 u_1g3157_134 (.O(n1g3157_134_o), .S(CLK), .Y0(ACCUMULATOR[5]), .Y1(n1g3157_124_o));  // open: out_4
  _1G3157 u_1g3157_135 (.O(n1g3157_135_o), .S(CLK), .Y0(ACCUMULATOR[6]), .Y1(n1g3157_125_o));  // open: out_4
  _1G3157 u_1g3157_136 (.O(n1g3157_136_o), .S(CLK), .Y0(ACCUMULATOR[7]), .Y1(n1g3157_126_o));  // open: out_4
  _1G3157 u_1g3157_137 (.O(n1g3157_137_o), .S(CLK), .Y0(ACCUMULATOR[8]), .Y1(n1g3157_127_o));  // open: out_4
  _1G3157 u_1g3157_138 (.O(n1g3157_138_o), .S(CLK), .Y0(ACCUMULATOR[9]), .Y1(n1g3157_128_o));  // open: out_4
  _1G3157 u_1g3157_139 (.O(n1g3157_139_o), .S(RUN_t), .Y0(Input_A[0]), .Y1(n1g3157_129_o));  // open: out_4
  _1G3157 u_1g3157_140 (.O(n1g3157_140_o), .S(RUN_t), .Y0(Input_A[1]), .Y1(n1g3157_130_o));  // open: out_4
  _1G3157 u_1g3157_141 (.O(n1g3157_141_o), .S(RUN_t), .Y0(Input_A[2]), .Y1(n1g3157_131_o));  // open: out_4
  _1G3157 u_1g3157_142 (.O(n1g3157_142_o), .S(RUN_t), .Y0(Input_A[3]), .Y1(n1g3157_132_o));  // open: out_4
  _1G3157 u_1g3157_143 (.O(n1g3157_143_o), .S(RUN_t), .Y0(Input_A[4]), .Y1(n1g3157_133_o));  // open: out_4
  _1G3157 u_1g3157_144 (.O(n1g3157_144_o), .S(RUN_t), .Y0(Input_A[5]), .Y1(n1g3157_134_o));  // open: out_4
  _1G3157 u_1g3157_145 (.O(n1g3157_145_o), .S(RUN_t), .Y0(Input_A[6]), .Y1(n1g3157_135_o));  // open: out_4
  _1G3157 u_1g3157_146 (.O(n1g3157_146_o), .S(RUN_t), .Y0(Input_A[7]), .Y1(n1g3157_136_o));  // open: out_4
  _1G3157 u_1g3157_147 (.O(n1g3157_147_o), .S(RUN_t), .Y0(1'b0), .Y1(n1g3157_137_o));  // open: out_4
  _1G3157 u_1g3157_148 (.O(n1g3157_148_o), .S(RUN_t), .Y0(1'b0), .Y1(n1g3157_138_o));  // open: out_4
  _1G3157 u_1g3157_149 (.O(ACCUMULATOR[0]), .S(n1g3157_139_o), .Y0(1'b0), .Y1(1'b1));  // open: out_4
  _1G3157 u_1g3157_150 (.O(ACCUMULATOR[1]), .S(n1g3157_140_o), .Y0(1'b0), .Y1(1'b1));  // open: out_4
  _1G3157 u_1g3157_151 (.O(ACCUMULATOR[2]), .S(n1g3157_141_o), .Y0(1'b0), .Y1(1'b1));  // open: out_4
  _1G3157 u_1g3157_152 (.O(ACCUMULATOR[3]), .S(n1g3157_142_o), .Y0(1'b0), .Y1(1'b1));  // open: out_4
  _1G3157 u_1g3157_153 (.O(ACCUMULATOR[4]), .S(n1g3157_143_o), .Y0(1'b0), .Y1(1'b1));  // open: out_4
  _1G3157 u_1g3157_154 (.O(ACCUMULATOR[5]), .S(n1g3157_144_o), .Y0(1'b0), .Y1(1'b1));  // open: out_4
  _1G3157 u_1g3157_155 (.O(ACCUMULATOR[6]), .S(n1g3157_145_o), .Y0(1'b0), .Y1(1'b1));  // open: out_4
  _1G3157 u_1g3157_156 (.O(ACCUMULATOR[7]), .S(n1g3157_146_o), .Y0(1'b0), .Y1(1'b1));  // open: out_4
  _1G3157 u_1g3157_157 (.O(ACCUMULATOR[8]), .S(n1g3157_147_o), .Y0(1'b0), .Y1(1'b1));  // open: out_4
  _1G3157 u_1g3157_158 (.O(ACCUMULATOR[9]), .S(n1g3157_148_o), .Y0(1'b0), .Y1(1'b1));  // open: out_4

  // Other names for the same wires on the sheet: A[7:0] = Input_A; B[4:0] = Input_B; RESULT[9:0] = ACCUMULATOR;
  //   X[4:0] = Input_X

  // Notes on the sheet:
  //   A + B*X
  //   A - B*X
  //   A / B
  //   SUB/ADD=off, DIV/MUL=off, Result in ACCUMULATOR 
  //   SUB/ADD=on, DIV/MUL=off, Result in ACCUMULATOR 
  //   SUB/ADD=on, DIV/MUL=on, X=0, Result in COUNT
  //   _
  //   _
endmodule

module Oscilator (
  input  E,
  output CK
);

  wire clock_1_out, d_ff_1_q;

  D_Flip_Flop #(.trigger("low")) d_ff_1 (.D(E), .clk(clock_1_out), .Q(d_ff_1_q));  // open: Qn, preset, reset
  Clock clock_1 (.out(clock_1_out));
  Pull_Resistor pull_resistor_1 (.node(d_ff_1_q));
  and and_1 (CK, d_ff_1_q, clock_1_out);
endmodule

module _1G3157 (
  input  S,
  input  Y0,
  input  Y1,
  output out_4,
  output O
);

  Pull_Resistor pull_resistor_1 (.node(S));
  Multiplexer #(.disabled("Z"), .enable("false")) multiplexer_1 (.in0(Y0), .in1(Y1), .out(O), .sel(S));
  Pull_Resistor pull_resistor_2 (.node(O));
  LED led_1 (.in(S));
  LED #(.active("false")) led_2 (.in(S));

  assign out_4 = S;
endmodule
